# Fritzing sketch bluetooth_car (saved by Fritzing 0.9.2b)
breadboards: 1

parts:
  Eleman1 = Arduino Uno (Rev3)
  M1 = DC Motor
  M2 = DC Motor  # not connected
  M3 = DC Motor  # not connected
  M4 = DC Motor
  S1 = H-Bridge with L298N
  Eleman2 = Bluetooth HC-06
  LED1 = LEDs [package=led10mm]
  LED2 = LEDs [package=led10mm]
  R1 = Resistor [tolerance=±5% resistance=220 package="2010 [SMD]"]
  LED3 = LED - 5mm [color="Red (633nm)" package="5 mm [THT]"]
  LED4 = LED - 5mm [color="Red (633nm)" package="5 mm [THT]"]
  R2 = Resistor [tolerance=±5% resistance=220 package="2010 [SMD]"]
  J1 = Piezo Speaker
  BAT1 = BC9VPC [package=bc9vpc]

nets:
  N1: Eleman1.D8, S1.IN2
  N2: Eleman1.D9_PWM, S1.IN1
  N3: Eleman1.D10_PWM/SS, S1.ENB
  N4: Eleman1.D11_PWM/MOSI, S1.ENA
  N5: Eleman1.D12/MISO, S1.IN4
  N6: Eleman1.D13/SCK, S1.IN3
  N7: Eleman1.D0/RX, Eleman2.TXD
  N8: Eleman1.D1/TX, Eleman2.RXD
  N9: Eleman1.D3_PWM, R1.Pin_0
  N10: Eleman1.D4, R2.Pin_0
  N11: Eleman1.D5_PWM, J1.pin2
  5V: Eleman1.5V, Eleman2.VCC
  GND: Eleman1.GND, S1.GND, Eleman2.GND, LED3.cathode, LED4.cathode, J1.pin1, BAT1.V-
  VIN: Eleman1.VIN, S1.12V, BAT1.V+
  N12: M1.pin_1, S1.M1-02
  N13: M1.pin_2, S1.M1-01
  N14: M4.pin_1, S1.M2-01
  N15: M4.pin_2, S1.M2-02
  N16: LED1.A, LED2.A
  N17: LED1.C, LED2.C, R1.Pin_1
  N18: LED3.anode, LED4.anode, R2.Pin_1

notes:
  Far Sağ
  Far Sol
  Korna
  ParkSağ
  Park Sol]
  HC-06'nın Rx ve Tx pinine voltaj bölücü dirençler koydum ve 3v3 verdim, bluetooth modulü kararsız çalıştı, komutları algılamadı, bazen algıladı, bazen algılamadı, Rx ve Tx'i direk bağladım ve 5v verdim, herhangi bir sorun çıkmadı ve gayet güzel ve kararlı çalıştı. Siz isterseniz önce voltaj bölücü direnç ve 3v3 verin, doğabilecek sorunlardan mesul değilim.

custom parts:
  H-Bridge with L298N: h-bridge
